# Fritzing sketch balloon_aq (saved by Fritzing 0.9.2b)
breadboards: 1

parts:
  R1 = Resistor [tolerance=±5% resistance=220 package=THT]
  Part1 = Arduino Uno (Rev3)
  Part2 = Gas Sensor Breakout Board
  AM1 = AM2302 Humidity and Temperature Sensor
  BMP1 = BMP085 Breakout
  R2 = Resistor [tolerance=±5% resistance=220 package="0603 [SMD]"]

nets:
  GND: R1.Pin_0, Part1.GND, Part2.GND, AM1.GND, BMP1.GND
  N1: R1.Pin_1, Part1.A0, Part2.B1
  N2: Part1.A4/SDA, BMP1.SCL
  N3: Part1.A5/SCL, BMP1.SDA
  N4: Part1.D3_PWM, AM1.DATA, R2.Pin_1
  5V: Part1.5V, Part2.A1, Part2.H1, AM1.VDD, BMP1.VIN, R2.Pin_0

custom parts:
  BMP085 Breakout: A breakout for the BMP085 barometric pressure and temperature sensor
